# Fritzing sketch shield_rgb_led (saved by Fritzing 1.0.4)

parts:
  Shield1 = Arduino Nano Shield V3
  Onderdeel1 = Arduino Nano RP2040 Connect  # not connected
  RGB1 = RGB-LED-module [package="5 mm [THT]"]
  Stekker1 = Dagu DGServo 9g header connector (female) [package=THT]

nets:
  N1: Shield1.D9~, RGB1.G
  N2: Shield1.D6~, RGB1.B
  N3: RGB1.R, Stekker1.pulse
  N4: RGB1.-, Stekker1.gnd

custom parts:
  Arduino Nano Shield V3: The Arduino Nano Shield is a compact and versatile accessory designed to simplify the development of Arduino Nano-based projects. This shield provides a convenient way to access all of the Nano's I/O pins, power connections, and additional features, making it ideal for prototyping and DIY electronics projects. Key Features: Pin Accessibility: Breaks out all 30 pins of the Arduino Nano to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
  RGB-LED-module: RGB-LED-module met gemeenschappelijke min: pinnen -, R, G en B.
